// Logisim project RAM Query.circ as structural Verilog
module Timer (
  input  in_1,
  input  in_2,
  input  in_3,
  input  [3:0] in_4,
  output out_5
);

  wire [3:0] counter_1_q;

  Counter #(.width(4), .max('hf)) counter_1 (
    .count(in_1), .Q(counter_1_q), .clk(in_3), .clr(in_2));  // open: load, D, carry
  Comparator #(.width(4)) comparator_1 (.a(in_4), .b(counter_1_q), .eq(out_5));  // open: gt, lt

  // Other names for the same wires on the sheet: clk = in_3; ready = out_5; reset = in_2; start = in_1;
  //   wait_time[3:0] = in_4

  // Notes on the sheet:
  //   Timer
endmodule

module Inverse (
  input  [31:0] in_1,
  output [31:0] out_2
);


  assign out_2 = {in_1[7:0], in_1[15:8], in_1[23:16], in_1[31:24]};

  // Notes on the sheet:
  //   Bytes Inverser
endmodule

module Read_Data (
  input  in_1
);
endmodule
